# Fritzing sketch weatherStation (saved by Fritzing 0.9.5d)
breadboards: 1

parts:
  OLED_I2C1 = OLED 128x64 I2C Monochrome Display
  DHT1 = DHT11 Humitidy and Temperature Sensor (3 pins)  # not connected
  U1 = NodeMCU V3.0

nets:
  N1: OLED_I2C1.SDA, U1.D2
  N2: OLED_I2C1.SCK, U1.D1
  VDD: OLED_I2C1.VDD, U1.3V3
  GND: OLED_I2C1.GND, U1.GND

custom parts:
  DHT11 Humitidy and Temperature Sensor (3 pins): DHT11 Humidity and Temperature Sensor (3 pins).
  NodeMCU V3.0: ESP8266 based NodeMCU
