# Fritzing sketch weatherStation2 (saved by Fritzing 0.9.5d)
breadboards: 2

parts:
  OLED_I2C1 = OLED 128x64 I2C Monochrome Display
  DHT1 = DHT11 Humitidy and Temperature Sensor (3 pins)  # not connected
  U1 = NodeMCU V3.0
  Sensor1 = Gas Sensor Breakout Board
  Part1 = Arduino Uno (Rev3)

nets:
  N1: OLED_I2C1.SDA, U1.D2
  N2: OLED_I2C1.SCK, U1.D1
  VDD: OLED_I2C1.VDD, U1.3V3
  GND: OLED_I2C1.GND, U1.GND, Sensor1.GND
  N3: U1.A0, Sensor1.AOUT
  5V: Sensor1.5V, Part1.5V

custom parts:
  DHT11 Humitidy and Temperature Sensor (3 pins): DHT11 Humidity and Temperature Sensor (3 pins).
  NodeMCU V3.0: ESP8266 based NodeMCU
  Gas Sensor Breakout Board: Gas sensor breakout board. Input voltage is 5V. Sensor output is available in analog and digital.
